// Logisim project CircuitoIntegrado.circ as structural Verilog: 1 circuit, main circuit main
module main (
  input  [15:0] in_1,
  output [3:0] out_2
);

  wire clock_1_out;
  wire [3:0] R0_data_out, R1_data_out;
  wire [15:0] main_1_out_3, multiplexer_1_out;

  Clock clock_1 (.out(clock_1_out));
  IR_main main_1 (.in_2(in_1), .in_1(clock_1_out), .out_3(main_1_out_3));
  Multiplexer #(.width(16)) multiplexer_1 (
    .in0(main_1_out_3), .in1({16{1'b0}}), .out(multiplexer_1_out), .sel(1'b0));  // open: en
  Register R0 (.Data_In(multiplexer_1_out[11:8]), .Clock(clock_1_out), .Data_Out(R0_data_out));
  Register R1 (.Data_In(multiplexer_1_out[7:4]), .Clock(clock_1_out), .Data_Out(R1_data_out));
  ULA ula_1 (
    .Entry_A(R0_data_out), .Entry_B(R1_data_out), .OPCODE(multiplexer_1_out[15:12]), .Out(out_2));  // open: Carry__iN, Carry_Out

  // Notes on the sheet:
  //   começando a integrar as partes
  //   - primeiros testes...
endmodule
